// Digital circuit 2bit adder.dig as structural Verilog
module _2bit_adder (
  input  A1,
  input  B1,
  input  A0,
  input  B0,
  input  _0
);

  wire add_1_c_o, add_1_s, add_2_c_o, add_2_s;

  Add add_1 (.a(A1), .b(B1), .c_i(add_2_c_o), .s(add_1_s), .c_o(add_1_c_o));
  LED led_1 (.in(add_1_c_o));
  LED led_2 (.in(add_1_s));
  LED led_3 (.in(add_2_s));
  Add add_2 (.a(A0), .b(B0), .c_i(_0), .s(add_2_s), .c_o(add_2_c_o));
endmodule
