// Digital circuit and-or-latch.dig as structural Verilog
module and_or_latch (
  input  in_1,
  input  in_2
);

  wire and_1_out, not_1_out, or_1_out;

  not not_1 (not_1_out, in_2);
  or or_1 (or_1_out, and_1_out, in_1);
  and and_1 (and_1_out, or_1_out, not_1_out);
  LED led_1 (.in(and_1_out));
endmodule
