// Digital circuit gated_latch.dig as structural Verilog
module gated_latch (
  input  DataIn,
  input  Enable,
  output DataOut
);

  wire and_1_out, and_2_out, not_1_out, not_2_out, or_1_out;

  not not_1 (not_1_out, DataIn);
  and and_1 (and_1_out, DataIn, Enable);
  and and_2 (and_2_out, not_1_out, Enable);
  not not_2 (not_2_out, and_2_out);
  or or_1 (or_1_out, DataOut, and_1_out);
  and and_3 (DataOut, or_1_out, not_2_out);
endmodule
