// Digital circuit selector.dig as structural Verilog
module selector (
  input  A_eq_1_B_eq_0,
  input  A,
  input  B,
  output out_4
);

  wire nand_1_out, nand_2_out, not_1_out;

  not not_1 (not_1_out, A_eq_1_B_eq_0);
  nand nand_1 (nand_1_out, A_eq_1_B_eq_0, A);
  nand nand_2 (nand_2_out, not_1_out, B);
  nand nand_3 (out_4, nand_1_out, nand_2_out);
endmodule
